// Logisim project zadanie_1.circ as structural Verilog: 1 circuit, main circuit main
module main (
  input  A,
  input  B,
  input  C,
  input  D,
  output Y,
  output Y___DNF,
  output Y___KNF,
  output Z,
  output Z___DNF,
  output Z___KNF
);

  wire and_1_out, and_2_out, and_3_out, and_4_out, and_5_out, and_6_out, and_7_out, nand_1_out, nand_2_out,
       nor_1_out, not_1_out, not_2_out, not_3_out, not_4_out, or_1_out, or_2_out, or_3_out, or_4_out,
       or_5_out, or_6_out, or_7_out;

  not not_1 (not_1_out, A);
  not not_2 (not_2_out, C);
  not not_3 (not_3_out, B);
  not not_4 (not_4_out, D);
  and and_1 (and_1_out, A, B);
  nand nand_1 (nand_1_out, C, not_4_out);
  and and_2 (and_2_out, A, B, D);
  and and_3 (and_3_out, A, B, not_2_out);
  and and_4 (and_4_out, C, not_1_out, not_4_out);
  and and_5 (and_5_out, C, not_3_out, not_4_out);
  or or_1 (or_1_out, A, C);
  or or_2 (or_2_out, A, not_4_out);
  or or_3 (or_3_out, B, C);
  or or_4 (or_4_out, B, not_4_out);
  or or_5 (or_5_out, D, not_1_out, not_3_out, not_2_out);
  nand nand_2 (nand_2_out, C, not_4_out);
  nor nor_1 (nor_1_out, B, D);
  and and_6 (and_6_out, C, not_3_out);
  and and_7 (and_7_out, B, not_2_out);
  or or_6 (or_6_out, B, C, D);
  or or_7 (or_7_out, D, not_3_out, not_2_out);
  xnor xnor_1 (Y, and_1_out, nand_1_out);
  or or_8 (Y___DNF, and_2_out, and_3_out, and_4_out, and_5_out);
  and and_8 (Y___KNF, or_1_out, or_2_out, or_3_out, or_4_out, or_5_out);
  xor xor_1 (Z, nand_2_out, nor_1_out);
  or or_9 (Z___DNF, and_6_out, and_7_out, D);
  and and_9 (Z___KNF, or_6_out, or_7_out);
endmodule
