// Logisim project 2_zadanie.circ as structural Verilog: 1 circuit, main circuit main
module main (
  input  a,
  input  b,
  input  c,
  input  d,
  output A_D,
  output B_D,
  output C_D,
  output D_D,
  output A_K,
  output B_K,
  output C_K,
  output D_K
);

  wire n_a_b_out, n_a_nb_out, n_b_c_out, n_b_nc_out, n_na_c_out, n_na_nc_out, na_2_out, na_out, nb_2_out,
       nb_out, nc_2_out, nc_out;

  nand na (na_out, a, a);
  nor na_2 (na_2_out, a, a);
  nand nb (nb_out, b, b);
  nor nb_2 (nb_2_out, b, b);
  nand nc (nc_out, c, c);
  nor nc_2 (nc_2_out, c, c);
  nand n_b_c (n_b_c_out, b, c);
  nand n_a_nb (n_a_nb_out, a, nb_out);
  nand n_b_nc (n_b_nc_out, b, nc_out);
  nand n_na_c (n_na_c_out, na_out, c);
  nor n_nb_nc (A_K, nb_2_out, nc_2_out);
  nor n_a_b (n_a_b_out, a, b);
  nor n_na_nc (n_na_nc_out, na_2_out, nc_2_out);
  nand n_n_b_c__n_b_c (A_D, n_b_c_out, n_b_c_out);
  nand n_n_b_nc__n_a_nb (B_D, n_a_nb_out, n_b_nc_out);
  nand n_n_b_nc__n_na_c (C_D, n_b_nc_out, n_na_c_out);
  nor n_na___n_nb_nc (B_K, A_K, na_2_out);
  nor n_n_a_b__n_na_nc (C_K, n_a_b_out, n_na_nc_out);

  assign D_D = d;
  assign D_K = d;

  // Notes on the sheet:
  //   DNF
  //   KNF
endmodule
