// Logisim project 3zadanie.circ as structural Verilog: 1 circuit, main circuit main
module main (
  input  X,
  input  Res,
  output Y
);

  wire CLK_out, j_k_ff_1_q, j_k_ff_2_q, j_k_ff_2_qn, j_k_ff_3_q, j_k_ff_3_qn, n_n_nX1_Z2_Z3__n_nX1_Z2_Z3_out,
       n_n_Z1_X__n_Z3_X_out, n_n_Z1_X__nZ3_out, n_nX1_Z2_Z3_out, n_nZ2_nX_out, n_nZ2_X_out, n_nZ3_X_out,
       n_Z1_X_out, n_Z1_Z3_X_out, n_Z3_X_out, nX_out;

  nand nX (nX_out, X, X);
  Clock CLK (.out(CLK_out));
  nand n_nX1_Z2_Z3 (n_nX1_Z2_Z3_out, nX_out, j_k_ff_2_q, j_k_ff_3_q);
  nand n_Z1_X (n_Z1_X_out, X, j_k_ff_1_q);
  nand n_Z3_X (n_Z3_X_out, X, j_k_ff_3_q);
  nand n_nZ3_X (n_nZ3_X_out, X, j_k_ff_3_qn);
  nand n_nZ2_X (n_nZ2_X_out, j_k_ff_2_qn, X);
  nand n_nZ2_nX (n_nZ2_nX_out, j_k_ff_2_qn, nX_out);
  nand n_n_nX1_Z2_Z3__n_nX1_Z2_Z3 (n_n_nX1_Z2_Z3__n_nX1_Z2_Z3_out, n_nX1_Z2_Z3_out, n_nX1_Z2_Z3_out);
  nand n_n_Z1_X__nZ3 (n_n_Z1_X__nZ3_out, n_Z1_X_out, j_k_ff_3_qn);
  nand n_n_Z1_X__n_Z3_X (n_n_Z1_X__n_Z3_X_out, n_Z3_X_out, n_Z1_X_out);
  nand n_Z1_Z3_X (n_Z1_Z3_X_out, j_k_ff_1_q, j_k_ff_3_q, X);
  nand n_n_Z1_Z3_X__n_Z1_Z3_X (Y, n_Z1_Z3_X_out, n_Z1_Z3_X_out);
  J_K_Flip_Flop j_k_ff_1 (
    .J(n_n_nX1_Z2_Z3__n_nX1_Z2_Z3_out), .clk(CLK_out), .K(n_n_Z1_X__nZ3_out), .Q(j_k_ff_1_q), .reset(Res));  // open: Qn, preset, en
  J_K_Flip_Flop j_k_ff_2 (
    .J(n_n_Z1_X__n_Z3_X_out), .clk(CLK_out), .K(n_nZ3_X_out), .Q(j_k_ff_2_q), .Qn(j_k_ff_2_qn), .reset(Res));  // open: preset, en
  J_K_Flip_Flop j_k_ff_3 (
    .J(n_nZ2_X_out), .clk(CLK_out), .K(n_nZ2_nX_out), .Q(j_k_ff_3_q), .Qn(j_k_ff_3_qn), .reset(Res));  // open: preset, en
endmodule
